// Logisim project 16 1 multiplexer using 8 1 multiplexer.circ as structural Verilog: 1 circuit, main circuit main
module main (
  input  in_1,
  input  S3,
  input  in_3,
  input  in_4,
  input  S2,
  input  in_6,
  input  in_7,
  input  S1,
  input  in_9,
  input  in_10,
  input  in_11,
  input  S0,
  input  in_13,
  input  Y,
  input  in_15,
  input  in_16,
  input  in_17,
  input  in_18,
  input  in_19,
  input  in_20,
  input  in_21,
  output out_22
);

  wire [7:0] multiplexer_1_out, multiplexer_2_out;
  wire [7:1] multiplexer_3_out, undriven, undriven_2, undriven_3, undriven_4, undriven_5, undriven_6,
       undriven_7, undriven_8, undriven_9, undriven_10, undriven_11, undriven_12, undriven_13, undriven_14,
       undriven_15, undriven_16;

  Multiplexer #(.select(3), .width(8)) multiplexer_1 (
    .in0({undriven, in_1}), .in1({undriven_2, in_3}), .in2({undriven_3, in_4}), .in3({undriven_4, in_6}),
    .in4({undriven_9, in_7}), .in5({undriven_5, in_9}), .in6({undriven_12, in_10}),
    .in7({undriven_14, in_11}), .out(multiplexer_1_out));  // open: sel, en
  Multiplexer #(.select(3), .width(8)) multiplexer_2 (
    .in0({undriven_6, in_13}), .in1({undriven_7, in_15}), .in2({undriven_8, in_16}),
    .in3({undriven_10, in_17}), .in4({undriven_13, in_18}), .in5({undriven_11, in_19}),
    .in6({undriven_15, in_20}), .in7({undriven_16, in_21}), .out(multiplexer_2_out));  // open: sel, en
  Multiplexer #(.width(8)) multiplexer_3 (
    .in0(multiplexer_1_out), .in1(multiplexer_2_out), .out({multiplexer_3_out, out_22}));  // open: sel, en
  // Pins of 1 and 8 bits meet at {undriven_5, in_9}
  // Pins of 1 and 8 bits meet at {undriven_11, in_19}
  // Pins of 1 and 8 bits meet at {undriven, in_1}
  // Pins of 1 and 8 bits meet at {undriven_2, in_3}
  // Pins of 1 and 8 bits meet at {undriven_3, in_4}
  // Pins of 1 and 8 bits meet at {undriven_4, in_6}
  // Pins of 1 and 8 bits meet at {undriven_9, in_7}
  // Pins of 1 and 8 bits meet at {undriven_12, in_10}
  // Pins of 1 and 8 bits meet at {undriven_14, in_11}
  // Pins of 1 and 8 bits meet at {undriven_6, in_13}
  // Pins of 1 and 8 bits meet at {undriven_7, in_15}
  // Pins of 1 and 8 bits meet at {undriven_8, in_16}
endmodule
